# Fritzing sketch nfc (saved by Fritzing 0.9.3b)

parts:
  Part1 = RFID-RC522 [part_number=101218]
  U1 = NodeMCU V3.0

nets:
  N1: Part1.SDA, U1.D4
  N2: Part1.SCK, U1.D5
  N3: Part1.MOSI, U1.D7
  N4: Part1.MISO, U1.D6
  GND: Part1.GND, U1.GND
  N5: Part1.RST, U1.D3
  3.3V: Part1.3.3V, U1.3V3

custom parts:
  NodeMCU V3.0: ESP8266 based NodeMCU
