# Fritzing sketch schematic (saved by Fritzing 0.9.3b)
breadboards: 1

parts:
  U1 = NodeMCU V3.0
  LED1 = LED - 5mm [color="Red (633nm)" package="5 mm [THT]"]

nets:
  N1: U1.D4, LED1.cathode
  N2: U1.GND, LED1.anode

custom parts:
  NodeMCU V3.0: ESP8266 based NodeMCU
